# Fritzing sketch arduino_style_analog_read (saved by Fritzing 0.8.4b)

parts:
  U1 = POT [package=pot_alpha_rv16af-20]
  Part2 = Espruino

nets:
  N1: U1.A, Part2.3.3
  N2: U1.S, Part2.C4
  N3: U1.E, Part2.GND

custom parts:
  Espruino: Espruino is an Interactive JavaScript interpreter for Microcontrollers, so you can program them quickly and easily. The Espruino Board on KickStarter is a specially designed computer with Espruino software pre-installed. It complements the Espruino software with masses of functionality and great battery life.
