# Fritzing sketch play_a_melody (saved by Fritzing 0.8.4b)

parts:
  Part1 = Espruino
  SP1 = SPEAKER [package=pcb_mount_speaker]

nets:
  N1: Part1.GND, SP1.+
  N2: Part1.A10, SP1.-

custom parts:
  Espruino: Espruino is an Interactive JavaScript interpreter for Microcontrollers, so you can program them quickly and easily. The Espruino Board on KickStarter is a specially designed computer with Espruino software pre-installed. It complements the Espruino software with masses of functionality and great battery life.
